# Fritzing sketch attiny (saved by Fritzing 0.9.10b)
breadboards: 1

parts:
  Power_plug1 = Power plug
  Power_plug2 = Power plug
  C2 = Ceramic Capacitor [capacitance=100nF voltage=35V package="100 mil [THT, multilayer]"]
  Bauteil3 = USB converter CP2102
  R5 = Resistor [tolerance=±5% power=0.25 resistance=4.7k package=THT]
  Bauteil4 = SMD Adapter
  R6 = Resistor [tolerance=±5% power=0.25 resistance=220 package=THT]
  S3 = Pushbutton [package="[THT]"]
  S4 = Glühbirne  # not connected
  Q2 = NPN-Transistor [package="TO92 [THT]"]
  R7 = Resistor [tolerance=±5% power=0.25 resistance=220 package=THT]
  LED1 = LED - 5mm [color="Green (560nm)" current=0.030 package="5 mm [THT]"]

nets:
  GND: Power_plug1.GND, Power_plug2.GND, C2.0, Bauteil3.GND, Bauteil4.pin_8, S3.Pin_3, S3.Pin_4, Q2.E
  VCC: Power_plug1.VCC, C2.1, Bauteil3.+5V, Bauteil4.pin1
  N1: Power_plug2.VCC, LED1.cathode
  N2: Bauteil3.TXO, R5.Pin_1
  N3: Bauteil3.RXI, R5.Pin_0, Bauteil4.pin_6
  N4: Bauteil4.pin_2, R6.Pin_0
  N5: Bauteil4.pin_5, S3.Pin_1, S3.Pin_2
  N6: Bauteil4.pin_7, R7.Pin_1
  N7: R6.Pin_1, Q2.B
  N8: R7.Pin_0, LED1.anode

notes:
  5 V
  12 V
  5 V siehe Text!

custom parts:
  Power plug: simple 3 wire power plug Florian Schäffer, blafusel.de
  SMD Adapter: SMD Adapter SO8 SOIC8 SOP
  Glühbirne: light bulb
